# Fritzing sketch rgb_led (saved by Fritzing 1.0.3b)
breadboards: 1

parts:
  Mod1 = Raspberry Pi Pico
  R1 = Resistor [tolerance=±5% power=0.25W resistance=100 package=THT]
  R2 = Resistor [tolerance=±5% power=0.25W resistance=100 package=THT]
  R3 = Resistor [tolerance=±5% power=0.25W resistance=100 package=THT]
  LED1 = RGB LED (com. cathode, rbg) [color="Red (633nm)" current=0.030A package="5 mm [THT]"]

nets:
  N1: Mod1.pin_3, Mod1.pin_8, Mod1.pin_13, Mod1.pin_18, Mod1.pin_23, Mod1.pin_28, Mod1.pin_33, Mod1.pin_38
  N2: Mod1.pin_17, R1.Pin_0
  N3: Mod1.pin_19, R2.Pin_0
  N4: Mod1.pin_20, R3.Pin_0
  N5: R1.Pin_1, LED1.red_anode
  N6: R2.Pin_1, LED1.blue_anode
  N7: R3.Pin_1, LED1.green_anode

custom parts:
  Raspberry Pi Pico: Raspberry Pi Pico. Based around the RP2040 microcontroller the Pico is a low cost microcontroller device bringing Raspberry Pi quality, cost, and easy of use to the microcontroller space. Jan 2021, Split part in to two versions: tht (this one) and SMD. This one will drill holes for a .1 in header in pcb to allow plugging in the module as well as providing pads to solder the module to the top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
